# Fritzing sketch Project Circuit Diagram (saved by Fritzing 0.9.3b)

parts:
  S1 = H-Bridge with L298N
  Part1 = Bluetooth HC-05 Macho
  M1 = fc-51 [package=THT]
  hc-sr1 = hc-sr04
  Part2 = Arduino Nano (Rev3.0)
  M3 = DC Motor
  M4 = DC Motor
  M5 = DC Motor
  M6 = DC Motor
  M7 = fc-51 [package=THT]
  VCC1 = Battery block 9V

nets:
  12V: S1.12V, Part2.VIN, VCC1.+
  N1: S1.GND, VCC1.-
  N2: S1.ENA, Part2.D5
  N3: S1.IN1, Part2.D3
  N4: S1.IN2, Part2.D4
  N5: S1.IN3, Part2.D8
  N6: S1.IN4, Part2.D7
  N7: S1.ENB, Part2.D6
  N8: S1.M1-01, M4.pin_2, M6.pin_2
  N9: S1.M1-02, M4.pin_1, M6.pin_1
  N10: S1.M2-01, M3.pin_2, M5.pin_2
  N11: S1.M2-02, M3.pin_1, M5.pin_1
  N12: Part1.TXD, Part2.D0/RX
  N13: Part1.RXD, Part2.D1/TX
  N14: M1.pin1, Part2.D11/MOSI
  N15: M1.pin3, Part2.5V
  N16: hc-sr1.Trig, Part2.D9
  N17: hc-sr1.Echo, Part2.D10
  N18: Part2.D12/MISO, M7.pin1

custom parts:
  H-Bridge with L298N: h-bridge
